# Fritzing sketch ir-5-buttons (saved by Fritzing 0.9.5d)
breadboards: 1

parts:
  Composant1 = Arduino Micro (Rev3)  # not connected
  Grove1 = Grove Infrared Emitter
  R1 = Resistor [tolerance=±5% resistance=10k package="0805 [SMD]"]
  R2 = Resistor [tolerance=±5% resistance=10k package="0805 [SMD]"]
  R3 = Resistor [tolerance=±5% resistance=10k package="0805 [SMD]"]
  R4 = Resistor [tolerance=±5% resistance=10k package="0805 [SMD]"]
  R5 = Resistor [tolerance=±5% resistance=10k package="0805 [SMD]"]
  S1 = Pushbutton [package="[THT]"]
  S2 = Pushbutton [package="[THT]"]
  S3 = Pushbutton [package="[THT]"]
  S4 = Pushbutton [package="[THT]"]
  S5 = Pushbutton [package="[THT]"]

nets:
  N1: Grove1.GND, R1.Pin_1, R2.Pin_1, R3.Pin_1, R4.Pin_1, R5.Pin_1
  N2: Grove1.VCC, S1.Pin_3, S1.Pin_4, S2.Pin_3, S2.Pin_4, S3.Pin_3, S3.Pin_4, S4.Pin_3, S4.Pin_4, S5.Pin_3, S5.Pin_4
  N3: R1.Pin_0, S4.Pin_1, S4.Pin_2
  N4: R2.Pin_0, S5.Pin_1, S5.Pin_2
  N5: R3.Pin_0, S3.Pin_1, S3.Pin_2
  N6: R4.Pin_0, S2.Pin_1, S2.Pin_2
  N7: R5.Pin_0, S1.Pin_1, S1.Pin_2
